// Logisim project Mini-Tarea 1.circ as structural Verilog: 1 circuit, main circuit main
module main (
  input  [7:0] in_1,
  input  [7:0] in_2,
  input  [7:0] in_3,
  input  [7:0] in_4,
  input  [7:0] in_5,
  input  [7:0] in_6,
  output [7:0] out_7,
  output [7:0] out_8
);

  wire [7:0] and_1_out, and_2_out, and_3_out, nor_1_out, nor_2_out, not_1_out, not_2_out, not_3_out,
       not_4_out, or_1_out, or_2_out;

  assign not_1_out = ~in_2;  // NOT_Gate not_1, 8 bits wide
  assign not_2_out = ~in_3;  // NOT_Gate not_2, 8 bits wide
  assign nor_1_out = ~(in_1 | in_2);  // NOR_Gate nor_1, 8 bits wide
  assign and_1_out = in_1 & in_3;  // AND_Gate and_1, 8 bits wide
  assign and_2_out = not_1_out & in_3;  // AND_Gate and_2, 8 bits wide
  assign nor_2_out = ~(in_1 | not_2_out);  // NOR_Gate nor_2, 8 bits wide
  assign or_1_out = nor_1_out | and_1_out;  // OR_Gate or_1, 8 bits wide
  assign or_2_out = and_2_out | nor_2_out;  // OR_Gate or_2, 8 bits wide
  assign not_3_out = ~in_4;  // NOT_Gate not_3, 8 bits wide
  assign not_4_out = ~in_5;  // NOT_Gate not_4, 8 bits wide
  assign out_7 = or_1_out | or_2_out;  // OR_Gate or_3, 8 bits wide
  assign and_3_out = not_3_out & not_4_out;  // AND_Gate and_3, 8 bits wide
  assign out_8 = and_3_out | in_6;  // OR_Gate or_4, 8 bits wide
endmodule
