// Logisim project Mini-tarea 2.circ as structural Verilog: 4 circuits, main circuit main
module main (
  input  in_1,
  output out_2
);

  wire circuitocombinacional_1_d0, circuitocombinacional_1_d1, clock_1_out, registro2bits_1_out_4,
       registro2bits_1_out_5;

  Clock clock_1 (.out(clock_1_out));
  registro2bits registro2bits_1 (
    .in_1(clock_1_out), .in_3(circuitocombinacional_1_d0), .out_4(registro2bits_1_out_4),
    .in_2(circuitocombinacional_1_d1), .out_5(registro2bits_1_out_5));
  circuitoCombinacional circuitocombinacional_1 (
    .q1(registro2bits_1_out_4), .q0(registro2bits_1_out_5), .x(in_1), .y(out_2),
    .d1(circuitocombinacional_1_d1), .d0(circuitocombinacional_1_d0));
endmodule

module registro2bits (
  input  in_1,
  input  in_2,
  input  in_3,
  output out_4,
  output out_5
);

  D_Flip_Flop d_ff_1 (.clk(in_1), .D(in_2), .Q(out_4));  // open: Qn, preset, en, reset
  D_Flip_Flop d_ff_2 (.clk(in_1), .D(in_3), .Q(out_5));  // open: Qn, preset, en, reset
endmodule

module circuitoCombinacional (
  input  q1,
  input  q0,
  input  x,
  output y,
  output d1,
  output d0
);

  d1 d1_1 (.q1(q1), .q0(q0), .x(x), .out_4(d1));
  and and_1 (y, q1, q0);

  assign d0 = x;
endmodule

module d1 (
  input  q1,
  input  q0,
  input  x,
  output out_4
);

  wire and_1_out, and_2_out, not_1_out, not_2_out;

  not not_1 (not_1_out, q0);
  not not_2 (not_2_out, x);
  and and_1 (and_1_out, q1, not_1_out, x);
  and and_2 (and_2_out, q0, not_2_out);
  or or_1 (out_4, and_1_out, and_2_out);
endmodule
