// Logisim project Mini tarea 3.circ as structural Verilog: 2 circuits, main circuit main
module main (
  input  x0,
  input  x1,
  input  OP1,
  input  OP0,
  output out_5
);

  wire and_1_out, clock_1_out, mux_1_out_7, nand_1_out, nor_1_out, or_1_out;

  and and_1 (and_1_out, x0, x1);
  or or_1 (or_1_out, x0, x1);
  nand nand_1 (nand_1_out, x0, x1);
  nor nor_1 (nor_1_out, x0, x1);
  Clock clock_1 (.out(clock_1_out));
  mux mux_1 (
    .in_1(and_1_out), .in_2(or_1_out), .in_3(nand_1_out), .in_4(nor_1_out), .OP1(OP1), .OP0(OP0),
    .out_7(mux_1_out_7));
  D_Flip_Flop #(.trigger("falling")) d_ff_1 (
    .clk(clock_1_out), .D(mux_1_out_7), .Q(out_5));  // open: Qn, preset, en, reset
endmodule

module mux (
  input  in_1,
  input  in_2,
  input  in_3,
  input  in_4,
  input  OP1,
  input  OP0,
  output out_7
);

  wire and_1_out, and_2_out, and_3_out, and_4_out, not_1_out, not_2_out;

  not not_1 (not_1_out, OP1);
  not not_2 (not_2_out, OP0);
  and and_1 (and_1_out, in_1, not_1_out, not_2_out);
  and and_2 (and_2_out, in_2, not_1_out, OP0);
  and and_3 (and_3_out, in_3, OP1, not_2_out);
  and and_4 (and_4_out, in_4, OP1, OP0);
  or or_1 (out_7, and_1_out, and_2_out, and_3_out, and_4_out);
endmodule
