// Logisim project tarea1.circ as structural Verilog: 10 circuits, main circuit reconocedor
module main (
);

  wire b, clock_2_out, clock_3_out, r;
  wire [1:0] direccion_1_out_3, direccion_2_out_3, joystick_1_x, joystick_1_y, random_1_out, random_2_out;
  wire [31:0] logicajuego_1_x, logicajuego_1_y;

  Button button_1 (.out(b));
  Clock clock_1 (.out(r));
  Clock #(.highDuration(3)) clock_2 (.out(clock_2_out));
  Clock #(.highDuration(2)) clock_3 (.out(clock_3_out));
  Random #(.width(2)) random_1 (.clk(clock_2_out), .out(random_1_out));  // open: next, clr
  direccion direccion_1 (.out_3(direccion_1_out_3), .in_1(random_1_out), .in_2(random_2_out));
  Random #(.width(2)) random_2 (.clk(clock_3_out), .out(random_2_out));  // open: next, clr
  Joystick #(.bits(2)) joystick_1 (.x(joystick_1_x), .y(joystick_1_y));
  direccion direccion_2 (.out_3(direccion_2_out_3), .in_1(joystick_1_x), .in_2(joystick_1_y));
  logicaJuego logicajuego_1 (
    .in_3(direccion_1_out_3), .in_5(direccion_2_out_3), .y(logicajuego_1_y), .x(logicajuego_1_x),
    .in_4({5{1'b1}}), .in_2(5'b00001), .in_1(32'h1030101), .in_6(b));
  DotMatrix #(.inputtype("row"), .matrixcols(4), .matrixrows(8)) dotmatrix_1 (
    .row0(logicajuego_1_y[3:0]), .row1(logicajuego_1_y[7:4]), .row2(logicajuego_1_y[11:8]),
    .row3(logicajuego_1_y[15:12]), .row4(logicajuego_1_y[19:16]), .row5(logicajuego_1_y[23:20]),
    .row6(logicajuego_1_y[27:24]), .row7(logicajuego_1_y[31:28]));
  DotMatrix #(.inputtype("row"), .matrixcols(4), .matrixrows(8)) dotmatrix_2 (
    .row0(logicajuego_1_x[3:0]), .row1(logicajuego_1_x[7:4]), .row2(logicajuego_1_x[11:8]),
    .row3(logicajuego_1_x[15:12]), .row4(logicajuego_1_x[19:16]), .row5(logicajuego_1_x[23:20]),
    .row6(logicajuego_1_x[27:24]), .row7(logicajuego_1_x[31:28]));

  // Notes on the sheet:
  //   Constantes
  //   Esta matriz muestra los movimientos del Pacman y Fantasma
  //   Esta matriz muestra los movimientos del Pacman comiendose la pepitas
endmodule

module reconocedor (
  input  [1:0] Horizontal,
  input  [1:0] Vertical,
  output [1:0] out_3,
  output out_4
);

  wire and_1_out, and_2_out, comparator_1_eq;
  wire [1:0] bit_extender_1_out, bit_extender_2_out, shifter_1_out;

  and and_1 (and_1_out, Horizontal[1], Vertical[0]);
  and and_2 (and_2_out, Horizontal[1], Vertical[1]);
  assign bit_extender_1_out = {{1{1'b0}}, and_1_out};  // Bit_Extender bit_extender_1
  Shifter #(.width(2)) shifter_1 (.in(bit_extender_1_out), .\dist (1'b1), .out(shifter_1_out));
  assign bit_extender_2_out = {{1{1'b0}}, and_2_out};  // Bit_Extender bit_extender_2
  Adder #(.width(2)) adder_1 (.a(shifter_1_out), .b(bit_extender_2_out), .out(out_3));  // open: cin, cout
  Comparator #(.width(2)) comparator_1 (.a(Horizontal), .b(Vertical), .eq(comparator_1_eq));  // open: gt, lt
  not not_1 (out_4, comparator_1_eq);

  // Other names for the same wires on the sheet: h[1:0] = Horizontal; v[1:0] = Vertical

  // Notes on the sheet:
  //   Codifica la direccion del joystick
endmodule

module direccion (
  input  [1:0] in_1,
  input  [1:0] in_2,
  output [1:0] out_3
);

  wire clock_1_out, reconocedor_1_out_4;
  wire [1:0] reconocedor_1_out_3, register_1_q;

  Clock clock_1 (.out(clock_1_out));
  Register #(.width(2)) register_1 (.D(out_3), .Q(register_1_q), .clk(clock_1_out));  // open: en, clr
  reconocedor reconocedor_1 (
    .out_3(reconocedor_1_out_3), .Vertical(in_2), .Horizontal(in_1), .out_4(reconocedor_1_out_4));
  Multiplexer #(.width(2)) multiplexer_1 (
    .in0(register_1_q), .in1(reconocedor_1_out_3), .out(out_3), .sel(reconocedor_1_out_4));  // open: en

  // Notes on the sheet:
  //   Entrega la direccion del joystick
endmodule

module calculoPosiciones (
  input  boton,
  input  [4:0] pos_incial,
  input  [1:0] direccion,
  output [4:0] out_4
);

  wire clock_1_out, reinicio;
  wire [4:0] adder_1_out, adder_2_out, multiplexer_1_out, register_1_q, subtractor_1_out, subtractor_2_out;

  Register #(.width(5)) register_1 (.D(out_4), .Q(register_1_q), .clk(clock_1_out));  // open: en, clr
  Clock clock_1 (.out(clock_1_out));
  not not_1 (reinicio, boton);
  Adder #(.width(5)) adder_1 (.a(register_1_q), .b(5'b00001), .out(adder_1_out));  // open: cin, cout
  Subtractor #(.width(5)) subtractor_1 (.a(register_1_q), .b(5'b00001), .out(subtractor_1_out));  // open: bin, bout
  Subtractor #(.width(5)) subtractor_2 (.a(register_1_q), .b(5'b00100), .out(subtractor_2_out));  // open: bin, bout
  Adder #(.width(5)) adder_2 (.a(register_1_q), .b(5'b00100), .out(adder_2_out));  // open: cin, cout
  Multiplexer #(.select(2), .width(5)) multiplexer_1 (
    .in0(adder_1_out), .in1(subtractor_1_out), .in2(subtractor_2_out), .in3(adder_2_out),
    .out(multiplexer_1_out), .sel(direccion));  // open: en
  Multiplexer #(.width(5)) multiplexer_2 (
    .in0(pos_incial), .in1(multiplexer_1_out), .out(out_4), .sel(reinicio));  // open: en

  // Other names for the same wires on the sheet: memoria[4:0] = out_4

  // Notes on the sheet:
  //   Boton de reinicio
  //   Mueve al Pacman dependiendo del sentido del joystick
  //   Constantes
endmodule

module pepitasOro (
  input  [31:0] pos_incial,
  input  boton,
  input  [4:0] in_3,
  output [31:0] out_4
);

  wire r, reinicio;
  wire [31:0] and_1_out, matrizPacman, not_1_out, register_1_q, shifter_1_out;

  Register #(.width(32)) register_1 (.D(out_4), .Q(register_1_q), .clk(r));  // open: en, clr
  assign not_1_out = ~matrizPacman;  // NOT_Gate not_1, 32 bits wide
  not not_2 (reinicio, boton);
  Shifter #(.width(32)) shifter_1 (.in(32'h1), .\dist (in_3), .out(shifter_1_out));
  assign and_1_out = not_1_out & register_1_q;  // AND_Gate and_1, 32 bits wide
  Register #(.width(32)) register_2 (.D(shifter_1_out), .Q(matrizPacman), .clk(r));  // open: en, clr
  Multiplexer #(.width(32)) multiplexer_1 (.in0(pos_incial), .in1(and_1_out), .out(out_4), .sel(reinicio));  // open: en
  Clock clock_1 (.out(r));

  // Other names for the same wires on the sheet: memoria[31:0] = out_4; posInit[31:0] = pos_incial;
  //   posPacman[4:0] = in_3

  // Notes on the sheet:
  //   Matriz inicial de las pepitas
  //   Cambia el valor de las pepitas si el Pacman se "come" una
  //   Boton de reinicio
  //   Calcula la matriz de posicion del Pacman
  //   Posicion del Pacman
  //   Reloj
endmodule

module estadoCeldas (
  input  [31:0] pepas,
  input  [4:0] Pacman,
  input  [4:0] Fantasma,
  output [31:0] out_4,
  output [31:0] out_5
);

  wire r;
  wire [31:0] generarmatriz_1_nuevox, generarmatriz_1_nuevoy, matrizFant, matrizPacman, shifter_1_out,
       shifter_2_out;

  Clock clock_1 (.out(r));
  generarMatriz generarmatriz_1 (
    .pepas(pepas), .Pacman(matrizPacman), .Fantasma(matrizFant), .nuevoY(generarmatriz_1_nuevoy),
    .nuevoX(generarmatriz_1_nuevox));
  Shifter #(.width(32)) shifter_1 (.in(32'h1), .\dist (Pacman), .out(shifter_1_out));
  Shifter #(.width(32)) shifter_2 (.in(32'h1), .\dist (Fantasma), .out(shifter_2_out));
  Register #(.width(32)) register_1 (.D(generarmatriz_1_nuevoy), .Q(out_4), .clk(r));  // open: en, clr
  Register #(.width(32)) register_2 (.D(generarmatriz_1_nuevox), .Q(out_5), .clk(r));  // open: en, clr
  Register #(.width(32)) register_3 (.D(shifter_1_out), .Q(matrizPacman), .clk(r));  // open: en, clr
  Register #(.width(32)) register_4 (.D(shifter_2_out), .Q(matrizFant), .clk(r));  // open: en, clr

  // Notes on the sheet:
  //   Calculo de los estados de las celdas
  //   generarMatriz
endmodule

module reinicio (
  input  boton_reinicio,
  input  pacman,
  input  pepitas,
  output out_4
);

  or or_1 (out_4, boton_reinicio, pacman, pepitas);

  // Notes on the sheet:
  //   Detector de reinicio
endmodule

module logicaJuego (
  input  [31:0] in_1,
  input  [4:0] in_2,
  input  [1:0] in_3,
  input  [4:0] in_4,
  input  [1:0] in_5,
  input  in_6,
  output [31:0] y,
  output [31:0] x
);

  wire clock_1_out, comparator_1_eq, comparator_2_eq, register_1_q, register_2_q, reinicio;
  wire [4:0] fantPos, pacmanPos;
  wire [31:0] matrizPepas;

  Comparator #(.width(5)) comparator_1 (.a(pacmanPos), .b(fantPos), .eq(comparator_1_eq));  // open: gt, lt
  calculoPosiciones calculoposiciones_1 (.boton(reinicio), .pos_incial(in_2), .out_4(fantPos), .direccion(in_3));
  calculoPosiciones calculoposiciones_2 (.boton(reinicio), .pos_incial(in_4), .out_4(pacmanPos), .direccion(in_5));
  Comparator #(.width(32)) comparator_2 (.a(matrizPepas), .b({32{1'b0}}), .eq(comparator_2_eq));  // open: gt, lt
  Clock clock_1 (.out(clock_1_out));
  Register #(.width(1)) register_1 (.D(comparator_1_eq), .Q(register_1_q), .clk(clock_1_out));  // open: en, clr
  Register #(.width(1)) register_2 (.D(comparator_2_eq), .Q(register_2_q), .clk(clock_1_out));  // open: en, clr
  pepitasOro pepitasoro_1 (.pos_incial(in_1), .boton(reinicio), .in_3(pacmanPos), .out_4(matrizPepas));
  estadoCeldas estadoceldas_1 (.pepas(matrizPepas), .Pacman(pacmanPos), .Fantasma(fantPos), .out_4(y), .out_5(x));
  reinicio reinicio_1 (.boton_reinicio(in_6), .out_4(reinicio), .pacman(register_1_q), .pepitas(register_2_q));
endmodule

module generarMatriz (
  input  [31:0] pepas,
  input  [31:0] Pacman,
  input  [31:0] Fantasma,
  output [31:0] nuevoY,
  output [31:0] nuevoX
);

  wire [31:0] not_1_out, or_1_out, or_2_out;

  assign or_1_out = {32{1'b0}} | Pacman;  // OR_Gate or_1, 32 bits wide
  assign or_2_out = pepas | Pacman;  // OR_Gate or_2, 32 bits wide
  assign nuevoY = or_1_out | Fantasma;  // OR_Gate or_3, 32 bits wide
  assign nuevoX = or_2_out & not_1_out;  // AND_Gate and_1, 32 bits wide
  assign not_1_out = ~Fantasma;  // NOT_Gate not_1, 32 bits wide

  // Notes on the sheet:
  //   Genera la matriz con los estados de las celdas
endmodule

module leds (
  input  [31:0] in_1
);

  wire [3:0] bit_extender_5_out;
  wire [15:0] _1, _2, _3, _4, bit_extender_1_out, bit_extender_2_out, bit_extender_3_out, bit_extender_4_out;
  wire [31:0] multiplier_1_out;

  DotMatrix #(.inputtype("row"), .matrixcols(4), .matrixrows(4)) dotmatrix_1 (
    .row0(4'b0111), .row1(4'b1010), .row2(4'b1110), .row3(4'b0111));
  assign bit_extender_1_out = {{12{1'b0}}, 4'b0111};  // Bit_Extender bit_extender_1
  assign bit_extender_2_out = {{12{1'b0}}, 4'b1010};  // Bit_Extender bit_extender_2
  assign bit_extender_3_out = {{12{1'b0}}, 4'b1110};  // Bit_Extender bit_extender_3
  assign bit_extender_4_out = {{12{1'b0}}, 4'b0111};  // Bit_Extender bit_extender_4
  Multiplier #(.width(32)) multiplier_1 (.a(in_1), .b(32'h2), .out(multiplier_1_out));  // open: cin, cout
  DotMatrix #(.inputtype("row"), .matrixcols(4), .matrixrows(4)) dotmatrix_2 (
    .row0(4'b1111), .row1(4'b1001), .row2(4'b1001), .row3(4'b1001));
  Bit_Extender #(.in_width(32), .out_width(4)) bit_extender_5 (.in(multiplier_1_out), .out(bit_extender_5_out));
  Shifter #(.width(16)) shifter_1 (.in(bit_extender_1_out), .\dist (bit_extender_5_out), .out(_1));
  Shifter #(.width(16)) shifter_2 (.in(bit_extender_2_out), .\dist (bit_extender_5_out), .out(_2));
  Shifter #(.width(16)) shifter_3 (.in(bit_extender_3_out), .\dist (bit_extender_5_out), .out(_3));
  Shifter #(.width(16)) shifter_4 (.in(bit_extender_4_out), .\dist (bit_extender_5_out), .out(_4));
  DotMatrix #(.inputtype("row"), .matrixcols(16), .matrixrows(32)) dotmatrix_3 (
    .row0(_1), .row1(_2), .row2(_3), .row3(_4));  // open: row4, row5, row6, row7, row8, row9, row10, row11, row12, row13, row14, row15, row16, row17, row18, row19, row20, row21, row22, row23, row24, row25, row26, row27, row28, row29, row30, row31
  DotMatrix #(.inputtype("row"), .matrixcols(4), .matrixrows(4)) dotmatrix_4 (
    .row0(4'b1111), .row1(4'b1111), .row2(4'b1111), .row3(4'b1111));

  // Other names for the same wires on the sheet: entry[31:0] = in_1

  // Notes on the sheet:
  //   Pacman
  //   Fantasma
  //   Pepita
endmodule
