// Logisim project Minitarea2.circ as structural Verilog: 4 circuits, main circuit d1
module circ_comb (
  input  x0,
  input  q1,
  input  q0,
  output y,
  output d1,
  output d0
);

  wire not_1_out;

  not not_1 (not_1_out, q1);
  d1 d1_1 (.x0(x0), .q1(q1), .q0(q0), .d1(d1));
  and and_1 (y, not_1_out, q0);

  assign d0 = x0;
endmodule

module d1 (
  input  x0,
  input  q1,
  input  q0,
  output d1
);

  wire and_1_out, not_1_out;

  not not_1 (not_1_out, q1);
  and and_1 (and_1_out, x0, not_1_out);
  or or_1 (d1, and_1_out, q0);
endmodule

module main (
  input  in_1,
  output out_2
);

  wire circ_comb_1_d0, circ_comb_1_d1, clock_1_out, memory_1_q0, memory_1_q1;

  memory memory_1 (.d1(circ_comb_1_d1), .d0(circ_comb_1_d0), .q1(memory_1_q1), .q0(memory_1_q0), .Reloj(clock_1_out));
  Clock clock_1 (.out(clock_1_out));
  circ_comb circ_comb_1 (
    .x0(in_1), .q1(memory_1_q1), .q0(memory_1_q0), .y(out_2), .d1(circ_comb_1_d1), .d0(circ_comb_1_d0));
endmodule

module memory (
  input  d1,
  input  d0,
  input  Reloj,
  output q1,
  output q0
);

  D_Flip_Flop #(.trigger("falling")) d_ff_1 (.clk(Reloj), .D(d1), .Q(q1));  // open: Qn, preset, en, reset
  D_Flip_Flop #(.trigger("falling")) d_ff_2 (.clk(Reloj), .D(d0), .Q(q0));  // open: Qn, preset, en, reset
endmodule
