// Logisim project Minitarea3.circ as structural Verilog: 1 circuit, main circuit main
module main (
  input  x0,
  input  x1,
  input  OP0,
  input  OP1,
  output z
);

  wire and_1_out, clock_1_out, multiplexer_1_out, not_1_out, not_2_out, or_1_out;

  and and_1 (and_1_out, x0, x1);
  or or_1 (or_1_out, x0, x1);
  not not_1 (not_1_out, and_1_out);
  not not_2 (not_2_out, or_1_out);
  Clock clock_1 (.out(clock_1_out));
  Multiplexer #(.select(2), .enable("false")) multiplexer_1 (
    .in0(and_1_out), .in1(or_1_out), .in2(not_1_out), .in3(not_2_out), .out(multiplexer_1_out),
    .sel({OP0, OP1}));
  D_Flip_Flop #(.trigger("falling")) d_ff_1 (
    .clk(clock_1_out), .D(multiplexer_1_out), .Q(z));  // open: Qn, preset, en, reset
endmodule
