// Logisim project tarea1.circ as structural Verilog: 15 circuits, main circuit main
module deco (
  input  x1,
  input  x0,
  output y0,
  output y1,
  output y2,
  output y3,
  output y4,
  output y5,
  output y6
);

  wire not_1_out;

  not not_1 (not_1_out, x0);
  or or_1 (y1, x1, x0);
  and and_1 (y4, x1, not_1_out);

  assign y0 = x1;
  assign y2 = x0;
  assign y3 = x1;
  assign y5 = 1'b0;
  assign y6 = x1;
endmodule

module main (
  output [1:0] out_1
);

  wire button_1_out, button_2_out, controlblock_1_inter;
  wire [1:0] controlblock_1_cursor_pos, memoryboard_1_out_4, memoryboard_1_out_5, memoryboard_1_out_6,
       memoryboard_1_out_7;
  wire [3:0] controlblock_1_leds_cursor, joystick_1_x, joystick_1_y;
  wire [6:0] decoblock_1_o0, decoblock_1_o1, decoblock_1_o2, decoblock_1_o3;

  Joystick joystick_1 (.x(joystick_1_x), .y(joystick_1_y));
  Button button_1 (.out(button_1_out));
  Button button_2 (.out(button_2_out));
  MemoryBoard memoryboard_1 (
    .joy_pos(controlblock_1_cursor_pos), .out_4(memoryboard_1_out_4), .out_5(memoryboard_1_out_5),
    .out_6(memoryboard_1_out_6), .out_7(memoryboard_1_out_7), .exchange(controlblock_1_inter),
    ._0_pos(out_1), .reset(button_2_out));
  ControlBlock controlblock_1 (
    .x(joystick_1_x), .y(joystick_1_y), .inter(controlblock_1_inter), .cursor_pos(controlblock_1_cursor_pos),
    .leds_cursor(controlblock_1_leds_cursor), ._0_pos(out_1), .button(button_1_out));
  _7_Segment_Display u_7_segment_display_1 (
    .g(decoblock_1_o0[6]), .f(decoblock_1_o0[5]), .a(decoblock_1_o0[0]), .b(decoblock_1_o0[1]),
    .e(decoblock_1_o0[4]), .d(decoblock_1_o0[3]), .c(decoblock_1_o0[2]), .dp(controlblock_1_leds_cursor[0]));
  _7_Segment_Display u_7_segment_display_2 (
    .g(decoblock_1_o2[6]), .f(decoblock_1_o2[5]), .a(decoblock_1_o2[0]), .b(decoblock_1_o2[1]),
    .e(decoblock_1_o2[4]), .d(decoblock_1_o2[3]), .c(decoblock_1_o2[2]), .dp(controlblock_1_leds_cursor[2]));
  _7_Segment_Display u_7_segment_display_3 (
    .g(decoblock_1_o1[6]), .f(decoblock_1_o1[5]), .a(decoblock_1_o1[0]), .b(decoblock_1_o1[1]),
    .e(decoblock_1_o1[4]), .d(decoblock_1_o1[3]), .c(decoblock_1_o1[2]), .dp(controlblock_1_leds_cursor[1]));
  _7_Segment_Display u_7_segment_display_4 (
    .g(decoblock_1_o3[6]), .f(decoblock_1_o3[5]), .a(decoblock_1_o3[0]), .b(decoblock_1_o3[1]),
    .e(decoblock_1_o3[4]), .d(decoblock_1_o3[3]), .c(decoblock_1_o3[2]), .dp(controlblock_1_leds_cursor[3]));
  DecoBlock decoblock_1 (
    .I0(memoryboard_1_out_7), .I1(memoryboard_1_out_6), .I2(memoryboard_1_out_5), .I3(memoryboard_1_out_4),
    .O0(decoblock_1_o0), .O1(decoblock_1_o1), .O2(decoblock_1_o2), .O3(decoblock_1_o3));
endmodule

module DecoBlock (
  input  [1:0] I0,
  input  [1:0] I1,
  input  [1:0] I2,
  input  [1:0] I3,
  output [6:0] O0,
  output [6:0] O1,
  output [6:0] O2,
  output [6:0] O3
);

  deco deco_1 (
    .y0(O0[0]), .y1(O0[1]), .y2(O0[2]), .y3(O0[3]), .y4(O0[4]), .y5(O0[5]), .y6(O0[6]), .x0(I0[0]), .x1(I0[1]));
  deco deco_2 (
    .y0(O1[0]), .y1(O1[1]), .y2(O1[2]), .y3(O1[3]), .y4(O1[4]), .y5(O1[5]), .y6(O1[6]), .x0(I1[0]), .x1(I1[1]));
  deco deco_3 (
    .y0(O2[0]), .y1(O2[1]), .y2(O2[2]), .y3(O2[3]), .y4(O2[4]), .y5(O2[5]), .y6(O2[6]), .x0(I2[0]), .x1(I2[1]));
  deco deco_4 (
    .y0(O3[0]), .y1(O3[1]), .y2(O3[2]), .y3(O3[3]), .y4(O3[4]), .y5(O3[5]), .y6(O3[6]), .x0(I3[0]), .x1(I3[1]));
endmodule

module vicinity (
  input  [1:0] P1,
  input  [1:0] P2,
  output out_3
);

  wire and_1_out, and_2_out, and_3_out, and_4_out, and_5_out, and_6_out, and_7_out, and_8_out, not_1_out,
       not_2_out, not_3_out, not_4_out;

  not not_1 (not_1_out, P1[1]);
  not not_2 (not_2_out, P1[0]);
  not not_3 (not_3_out, P2[1]);
  not not_4 (not_4_out, P2[0]);
  and and_1 (and_1_out, not_1_out, not_2_out, not_3_out, P2[0]);
  and and_2 (and_2_out, not_1_out, not_2_out, P2[1], not_4_out);
  and and_3 (and_3_out, not_1_out, P1[0], not_3_out, not_4_out);
  and and_4 (and_4_out, not_1_out, P1[0], P2[1], P2[0]);
  and and_5 (and_5_out, P1[1], P1[0], not_3_out, P2[0]);
  or or_1 (out_3, and_1_out, and_2_out, and_3_out, and_4_out, and_5_out, and_6_out, and_7_out, and_8_out);
  and and_6 (and_6_out, P1[1], P1[0], P2[1], not_4_out);
  and and_7 (and_7_out, P1[1], not_2_out, not_3_out, not_4_out);
  and and_8 (and_8_out, P1[1], not_2_out, P2[1], P2[0]);
endmodule

module CursorControl (
  input  [3:0] y,
  input  [3:0] x,
  output [1:0] out_3
);

  wire clock_1_out, comparator_1_lt, comparator_2_gt, comparator_3_gt, comparator_4_lt;
  wire [1:0] magic_1_out_6;

  Comparator #(.width(4), .mode("unsigned")) comparator_1 (.a(y), .b(4'b0100), .lt(comparator_1_lt));  // open: gt, eq
  Comparator #(.width(4), .mode("unsigned")) comparator_2 (.a(y), .b(4'b1100), .gt(comparator_2_gt));  // open: eq, lt
  Comparator #(.width(4), .mode("unsigned")) comparator_3 (.a(x), .b(4'b1100), .gt(comparator_3_gt));  // open: eq, lt
  Comparator #(.width(4), .mode("unsigned")) comparator_4 (.a(x), .b(4'b0100), .lt(comparator_4_lt));  // open: gt, eq
  magic magic_1 (
    .x3(comparator_1_lt), .x2(comparator_2_gt), .x1(comparator_3_gt), .x0(comparator_4_lt), .q(out_3),
    .out_6(magic_1_out_6));
  Register #(.width(2)) register_1 (.D(magic_1_out_6), .Q(out_3), .clk(clock_1_out));  // open: en, clr
  Clock clock_1 (.out(clock_1_out));

  // Notes on the sheet:
  //   Up
  //   Down
  //   Right
  //   Left
endmodule

module magic_d0 (
  input  x3,
  input  x2,
  input  x1,
  input  x0,
  input  q1,
  input  q0,
  output out_7
);

  wire and_1_out, and_2_out, and_3_out, and_4_out, and_5_out, not_1_out, not_2_out, not_3_out;

  not not_1 (not_1_out, x3);
  not not_2 (not_2_out, x2);
  not not_3 (not_3_out, x0);
  and and_1 (and_1_out, not_1_out, not_2_out, x1, not_3_out);
  and and_2 (and_2_out, not_1_out, x1, x0, q0);
  and and_3 (and_3_out, x2, x0, q0);
  and and_4 (and_4_out, x3, x0, q0);
  or or_1 (out_7, and_1_out, and_2_out, and_4_out, and_3_out, and_5_out);
  and and_5 (and_5_out, not_3_out, q0);
endmodule

module magic_d1 (
  input  x3,
  input  x2,
  input  x1,
  input  x0,
  input  q1,
  input  q0,
  output out_7
);

  wire and_1_out, and_2_out, and_3_out, and_4_out, and_5_out, and_6_out, not_1_out, not_3_out, not_4_out;

  not not_1 (not_1_out, x3);
  // NOT_Gate not_2 has open pins: in=x2, out=open
  not not_3 (not_3_out, x1);
  not not_4 (not_4_out, x0);
  and and_1 (and_1_out, not_1_out, x2, not_3_out, not_4_out);
  and and_2 (and_2_out, not_1_out, x2, not_3_out, q1);
  and and_3 (and_3_out, x3, x1, q1);
  and and_4 (and_4_out, x2, not_3_out, q1);
  or or_1 (out_7, and_1_out, and_2_out, and_3_out, and_4_out, and_5_out, and_6_out);
  and and_5 (and_5_out, not_1_out, q1);
  and and_6 (and_6_out, x0, q1);
endmodule

module magic (
  input  x3,
  input  x2,
  input  x1,
  input  x0,
  input  [1:0] q,
  output [1:0] out_6
);

  magic_d1 magic_d1_1 (.x3(x3), .x2(x2), .x1(x1), .x0(x0), .q1(q[1]), .q0(q[0]), .out_7(out_6[1]));
  magic_d0 magic_d0_1 (.x3(x3), .x2(x2), .x1(x1), .x0(x0), .q1(q[1]), .q0(q[0]), .out_7(out_6[0]));
endmodule

module ControlBlock (
  input  [3:0] x,
  input  [3:0] y,
  input  button,
  input  [1:0] _0_pos,
  output [3:0] leds_cursor,
  output [1:0] cursor_pos,
  output inter
);

  wire vicinity_1_out_3;

  CursorControl cursorcontrol_1 (.x(x), .y(y), .out_3(cursor_pos));
  vicinity vicinity_1 (.P1(cursor_pos), .P2(_0_pos), .out_3(vicinity_1_out_3));
  selector_2x4 selector_2x4_1 (
    .in_1(cursor_pos), .out_2(leds_cursor[3]), .out_3(leds_cursor[2]), .out_4(leds_cursor[1]),
    .out_5(leds_cursor[0]));
  Multiplexer #(.enable("false")) multiplexer_1 (.in0(1'b0), .in1(vicinity_1_out_3), .out(inter), .sel(button));
endmodule

module exchanger (
  input  [1:0] in_1,
  input  [1:0] in_2,
  input  [1:0] in_3,
  input  [1:0] in_4,
  input  [1:0] in_5,
  input  [1:0] in_6,
  output [1:0] out_7,
  output [1:0] out_8,
  output [1:0] out_9,
  output [1:0] out_10
);

  wire clock_1_out;
  wire [1:0] demultiplexer_1_out0, demultiplexer_1_out1, demultiplexer_1_out2, demultiplexer_1_out3,
       demultiplexer_2_out0, demultiplexer_2_out1, demultiplexer_2_out2, demultiplexer_2_out3,
       multiplexer_1_out, multiplexer_2_out, register_1_q, register_2_q;

  Multiplexer #(.select(2), .width(2), .enable("false")) multiplexer_1 (
    .in0(in_2), .in1(in_3), .in2(in_4), .in3(in_5), .out(multiplexer_1_out), .sel(in_1));
  Multiplexer #(.select(2), .width(2), .enable("false")) multiplexer_2 (
    .in0(in_2), .in1(in_3), .in2(in_4), .in3(in_5), .out(multiplexer_2_out), .sel(in_6));
  Register #(.width(2)) register_1 (.D(multiplexer_1_out), .Q(register_1_q), .clk(clock_1_out));  // open: en, clr
  Register #(.width(2)) register_2 (.D(multiplexer_2_out), .Q(register_2_q), .clk(clock_1_out));  // open: en, clr
  Clock clock_1 (.out(clock_1_out));
  Demultiplexer #(.select(2), .width(2), .enable("false")) demultiplexer_1 (
    .out0(demultiplexer_1_out0), .out1(demultiplexer_1_out1), .out2(demultiplexer_1_out2),
    .out3(demultiplexer_1_out3), .in(register_1_q), .sel(in_6));
  Demultiplexer #(.select(2), .width(2), .enable("false")) demultiplexer_2 (
    .out0(demultiplexer_2_out0), .out1(demultiplexer_2_out1), .out2(demultiplexer_2_out2),
    .out3(demultiplexer_2_out3), .in(register_2_q), .sel(in_1));
  assign out_7 = demultiplexer_1_out0 | demultiplexer_2_out0;  // OR_Gate or_1, 2 bits wide
  assign out_8 = demultiplexer_1_out1 | demultiplexer_2_out1;  // OR_Gate or_2, 2 bits wide
  assign out_9 = demultiplexer_1_out2 | demultiplexer_2_out2;  // OR_Gate or_3, 2 bits wide
  assign out_10 = demultiplexer_1_out3 | demultiplexer_2_out3;  // OR_Gate or_4, 2 bits wide
endmodule

module RegisterBank (
  input  [1:0] in_1,
  input  select_3,
  input  [1:0] in_3,
  input  select_2,
  input  [1:0] in_5,
  input  select_1,
  input  [1:0] in_7,
  input  select_0,
  input  reset,
  output [1:0] out_10,
  output [1:0] out_11,
  output [1:0] out_12,
  output [1:0] out_13
);

  wire clock_1_out, or_1_out, or_2_out, or_3_out, or_4_out;
  wire [1:0] multiplexer_1_out, multiplexer_2_out, multiplexer_3_out, multiplexer_4_out;

  Clock clock_1 (.out(clock_1_out));
  or or_1 (or_1_out, reset, select_3);
  or or_2 (or_2_out, reset, select_2);
  or or_3 (or_3_out, reset, select_1);
  or or_4 (or_4_out, reset, select_0);
  Multiplexer #(.width(2), .enable("false")) multiplexer_1 (
    .in0(in_1), .in1(2'b11), .out(multiplexer_1_out), .sel(reset));
  Multiplexer #(.width(2), .enable("false")) multiplexer_2 (
    .in0(in_3), .in1(2'b10), .out(multiplexer_2_out), .sel(reset));
  Multiplexer #(.width(2), .enable("false")) multiplexer_3 (
    .in0(in_5), .in1(2'b01), .out(multiplexer_3_out), .sel(reset));
  Multiplexer #(.width(2), .enable("false")) multiplexer_4 (
    .in0(in_7), .in1(2'b00), .out(multiplexer_4_out), .sel(reset));
  Register #(.width(2)) _11_value (.D(multiplexer_1_out), .en(or_1_out), .Q(out_10), .clk(clock_1_out));  // open: clr
  Register #(.width(2)) _10_value (.D(multiplexer_2_out), .en(or_2_out), .Q(out_11), .clk(clock_1_out));  // open: clr
  Register #(.width(2)) _01_value (.D(multiplexer_3_out), .en(or_3_out), .Q(out_12), .clk(clock_1_out));  // open: clr
  Register #(.width(2)) _00_value (.D(multiplexer_4_out), .en(or_4_out), .Q(out_13), .clk(clock_1_out));  // open: clr
endmodule

module selector_2x4 (
  input  [1:0] in_1,
  output out_2,
  output out_3,
  output out_4,
  output out_5
);

  wire not_1_out, not_2_out;

  and and_1 (out_2, in_1[1], in_1[0]);
  and and_2 (out_3, not_2_out, in_1[1]);
  not not_1 (not_1_out, in_1[1]);
  not not_2 (not_2_out, in_1[0]);
  and and_3 (out_5, not_2_out, not_1_out);
  and and_4 (out_4, in_1[0], not_1_out);
endmodule

module selector (
  input  [1:0] in_1,
  input  [1:0] in_2,
  output out_3,
  output out_4,
  output out_5,
  output out_6
);

  wire selector_2x4_1_out_2, selector_2x4_1_out_3, selector_2x4_1_out_4, selector_2x4_1_out_5,
       selector_2x4_2_out_2, selector_2x4_2_out_3, selector_2x4_2_out_4, selector_2x4_2_out_5;

  selector_2x4 selector_2x4_1 (
    .in_1(in_1), .out_2(selector_2x4_1_out_2), .out_3(selector_2x4_1_out_3), .out_4(selector_2x4_1_out_4),
    .out_5(selector_2x4_1_out_5));
  selector_2x4 selector_2x4_2 (
    .in_1(in_2), .out_2(selector_2x4_2_out_2), .out_3(selector_2x4_2_out_3), .out_4(selector_2x4_2_out_4),
    .out_5(selector_2x4_2_out_5));
  or or_1 (out_3, selector_2x4_1_out_2, selector_2x4_2_out_2);
  or or_2 (out_4, selector_2x4_1_out_3, selector_2x4_2_out_3);
  or or_3 (out_5, selector_2x4_1_out_4, selector_2x4_2_out_4);
  or or_4 (out_6, selector_2x4_1_out_5, selector_2x4_2_out_5);
endmodule

module MemoryBoard (
  input  reset,
  input  exchange,
  input  [1:0] joy_pos,
  output [1:0] out_4,
  output [1:0] out_5,
  output [1:0] out_6,
  output [1:0] out_7,
  output [1:0] _0_pos
);

  wire and_1_out, and_2_out, and_3_out, and_4_out, selector_1_out_3, selector_1_out_4, selector_1_out_5,
       selector_1_out_6;
  wire [1:0] exchanger_1_out_7, exchanger_1_out_8, exchanger_1_out_9, exchanger_1_out_10;

  selector selector_1 (
    .in_1(joy_pos), .in_2(_0_pos), .out_3(selector_1_out_3), .out_4(selector_1_out_4),
    .out_5(selector_1_out_5), .out_6(selector_1_out_6));
  exchanger exchanger_1 (
    .in_2(out_7), .in_3(out_6), .in_4(out_5), .in_5(out_4), .out_9(exchanger_1_out_9),
    .out_10(exchanger_1_out_10), .in_1(joy_pos), .in_6(_0_pos), .out_8(exchanger_1_out_8),
    .out_7(exchanger_1_out_7));
  and and_1 (and_1_out, exchange, selector_1_out_3);
  and and_2 (and_2_out, exchange, selector_1_out_4);
  RegisterBank registerbank_1 (
    .in_7(exchanger_1_out_7), .select_1(and_4_out), .select_0(and_3_out), .select_2(and_2_out),
    .select_3(and_1_out), .out_10(out_4), .out_11(out_5), .out_12(out_6), .out_13(out_7),
    .in_5(exchanger_1_out_8), .in_1(exchanger_1_out_10), .in_3(exchanger_1_out_9), .reset(reset));
  and and_3 (and_3_out, exchange, selector_1_out_6);
  and and_4 (and_4_out, exchange, selector_1_out_5);
  ZeroCalc zerocalc_1 (.in_1(out_4), .in_2(out_5), .in_3(out_6), .in_4(out_7), .out_5(_0_pos));
endmodule

module ZeroCalc (
  input  [1:0] in_1,
  input  [1:0] in_2,
  input  [1:0] in_3,
  input  [1:0] in_4,
  output [1:0] out_5
);

  wire comparator_1_eq, comparator_2_eq, comparator_3_eq, comparator_4_eq;
  wire [1:0] multiplexer_1_out, multiplexer_2_out, multiplexer_3_out, multiplexer_4_out;

  Comparator #(.width(2)) comparator_1 (.a(in_1), .b(2'b00), .eq(comparator_1_eq));  // open: gt, lt
  Comparator #(.width(2)) comparator_2 (.a(in_2), .b(2'b00), .eq(comparator_2_eq));  // open: gt, lt
  Comparator #(.width(2)) comparator_3 (.a(in_3), .b(2'b00), .eq(comparator_3_eq));  // open: gt, lt
  Comparator #(.width(2)) comparator_4 (.a(in_4), .b(2'b00), .eq(comparator_4_eq));  // open: gt, lt
  Multiplexer #(.width(2), .enable("false")) multiplexer_1 (
    .in0(2'b00), .in1(2'b11), .out(multiplexer_1_out), .sel(comparator_1_eq));
  Multiplexer #(.width(2), .enable("false")) multiplexer_2 (
    .in0(2'b00), .in1(2'b10), .out(multiplexer_2_out), .sel(comparator_2_eq));
  Multiplexer #(.width(2), .enable("false")) multiplexer_3 (
    .in0(2'b00), .in1(2'b01), .out(multiplexer_3_out), .sel(comparator_3_eq));
  Multiplexer #(.width(2), .enable("false")) multiplexer_4 (
    .in0(2'b00), .in1(2'b00), .out(multiplexer_4_out), .sel(comparator_4_eq));
  assign out_5 = multiplexer_1_out | multiplexer_2_out | multiplexer_3_out | multiplexer_4_out;  // OR_Gate or_1, 2 bits wide
endmodule
